// Logisim project cpu.circ as structural Verilog: 1 circuit, main circuit cpu
module cpu (
  input  clk,
  input  [31:0] Instruction,
  input  [31:0] MemReadData,
  output [31:0] MemAddress,
  output [31:0] ProgramCounter,
  output [31:0] ra,
  output [31:0] sp,
  output [31:0] t0,
  output [31:0] t1,
  output [31:0] t2,
  output [31:0] s0,
  output [31:0] s1,
  output [31:0] a0,
  output [3:0] MemWriteMask,
  output [31:0] MemWriteData
);

  wire control_logic_1_bsel, control_logic_1_regwen, regfile_1_p7, regfile_1_p8, regfile_1_p10,
       regfile_1_p22, regfile_1_p24;
  wire [2:0] control_logic_1_immsel;
  wire [3:0] control_logic_1_alusel;
  wire [31:0] adder_1_out, imm_gen_1_immediate, multiplexer_1_out, regfile_1_p4, regfile_1_p19, regfile_1_p20;

  Register #(.width(32)) PC (.D(adder_1_out), .clk(clk), .Q(ProgramCounter));  // open: en, clr
  Adder #(.width(32)) adder_1 (.a(ProgramCounter), .b(32'h4), .out(adder_1_out));  // open: cin, cout
  control_logic control_logic_1 (
    .RegWEn(control_logic_1_regwen), .ImmSel(control_logic_1_immsel), .BSel(control_logic_1_bsel),
    .ALUSel(control_logic_1_alusel), .Instruction(Instruction));  // open: PCSel, BrUn, ASel, MemWEn, WBSel, BrEq, BrLt
  // regfile regfile_1: pin names not known; wires that end beside it: Instruction[19:15], Instruction[24:20], Instruction[11:7], regfile_1_p4, control_logic_1_regwen, clk, regfile_1_p7, regfile_1_p8, regfile_1_p8, regfile_1_p10, ra, sp, t0, t1, t2, s0, s1, a0, regfile_1_p19, regfile_1_p20, regfile_1_p10, regfile_1_p22, regfile_1_p22, regfile_1_p24, regfile_1_p24
  imm_gen imm_gen_1 (.Instruction(Instruction), .ImmSel(control_logic_1_immsel), .Immediate(imm_gen_1_immediate));
  Multiplexer #(.enable("false"), .width(32)) multiplexer_1 (
    .in0(regfile_1_p20), .in1(imm_gen_1_immediate), .out(multiplexer_1_out), .sel(control_logic_1_bsel));
  alu alu_1 (.ALUResult(regfile_1_p4), .A(regfile_1_p19), .B(multiplexer_1_out), .ALUSel(control_logic_1_alusel));
  // partial_store partial_store_1: pin names not known
  // partial_load partial_load_1: pin names not known
  // branch_comp branch_comp_1: pin names not known

  // Notes on the sheet:
  //   To IMEM
  //   IMEM (do **NOT** move this)
  //   From IMEM
  //   Inputs/Outputs for testing. Do **NOT** move these.
  //   To DMEM
  //   DMEM (do **NOT** move this)
  //   From DMEM
endmodule
